# Fritzing sketch MR-990 (saved by Fritzing 1.0.3b)
breadboards: 1

parts:
  DIN1 = DIN-5 jack (MIDI) [package=THT]
  Componente1 = Arduino Mega 2560 (Rev3)
  R1 = Resistor [tolerance=±5% resistance=220 package="0805 [SMD]"]
  microSD1 = MicroSD Card Module

nets:
  N1: DIN1.5, Componente1.D18/TX1
  GND: DIN1.2, Componente1.GND, microSD1.GND
  N2: DIN1.4, R1.Pin_0
  5V: Componente1.5V, R1.Pin_1, microSD1.VCC
